# Fritzing sketch RFID-V2-3 (saved by Fritzing 0.9.3b)

parts:
  Componente1 = Arduino Uno (Rev3) - ICSP
  Part3 = RFID-RC522-v2
  R1 = Resistor [tolerance=±5% resistance=330k package=THT]
  J1 = Piezo Speaker
  LED1 = smd LED [color="Red (633nm)" package="0603 [SMD]"]
  LED2 = smd LED [color="Green (555nm)" package="0603 [SMD]"]
  R2 = Resistor [tolerance=±5% resistance=220 package=THT]
  R3 = Resistor [tolerance=±5% resistance=220 package=THT]

nets:
  N1: Componente1.ICSP_MISO, Componente1.D12/MISO, Part3.MISO
  N2: Componente1.D9_PWM, Part3.RST
  N3: Componente1.D10_PWM/SS, Part3.SDA
  N4: Componente1.D11_PWM/MOSI, Part3.MOSI
  N5: Componente1.D13/SCK, Part3.SCK
  GND: Componente1.GND, Part3.GND, J1.pin1, LED1.anode, LED2.anode
  N6: Componente1.D3_PWM, R1.Pin_1
  N7: Componente1.D5_PWM, R3.Pin_0
  N8: Componente1.D6_PWM, R2.Pin_0
  N9: Componente1.3V3, Part3.3_3V

custom parts:
  RFID-RC522-v2: A simple China made RFID-RC522 Reader; do check the pin labels, as this is a MFRC522 based clone.
